# Fritzing sketch Beacon (saved by Fritzing 0.9.3b)
perfboards: 1

parts:
  U1 = TRANSISTOR_NPN_2 [package=to-92]
  R1 = Resistor [tolerance=±5% resistance=220 package="1206 [SMD]"]
  R2 = Resistor [tolerance=±5% resistance=220 package="1206 [SMD]"]
  R3 = Resistor [tolerance=±5% resistance=220 package="1206 [SMD]"]
  R4 = Resistor [tolerance=±5% resistance=220 package="1206 [SMD]"]
  R5 = Resistor [tolerance=±5% resistance=220 package="1206 [SMD]"]
  Part1 = Arduino Nano (Rev3.0) (ICSP)
  Part2 = NRF24L01+ Breakout Board
  Part3 = LilyPad Buzzer
  LED2 = smd LED [color="Red (633nm)" package="1206 [SMD]"]
  LED3 = smd LED [color="Red (633nm)" package="1206 [SMD]"]
  LED4 = smd LED [color="Red (633nm)" package="1206 [SMD]"]
  LED5 = smd LED [color="Red (633nm)" package="1206 [SMD]"]
  BAT1 = BC9VPC [package=bc9vpc]

nets:
  N1: U1.C, Part3.+
  N2: U1.B, R1.Pin_0
  N3: U1.E, Part1.VIN, BAT1.V+
  N4: R1.Pin_1, Part1.D3
  N5: R2.Pin_0, LED2.anode
  N6: R3.Pin_0, LED3.anode
  N7: R3.Pin_1, Part1.D4
  N8: R4.Pin_0, LED4.anode
  N9: R5.Pin_0, LED5.anode
  N10: R5.Pin_1, Part1.D5
  GND: Part1.GND, Part2.GND, LED2.cathode, LED3.cathode
  N11: Part1.D7, Part2.CE
  N12: Part1.D8, Part2.CS
  N13: Part1.D11/MOSI, Part2.MOSI
  N14: Part1.D12/MISO, Part2.MISO
  3V3: Part1.3V3, Part2.VCC
  N15: LED4.cathode, LED5.cathode
